# Fritzing sketch l298n-arduino (saved by Fritzing 0.9.3b)

parts:
  L298N1 = L298N DC motor driver
  M1 = DC Motor
  M2 = DC Motor
  Part1 = Arduino Uno (Rev3)
  U1 = LIPO-2000mAh [package=lipo-2000]
  U2 = LIPO-2000mAh [package=lipo-2000]
  hc-sr1 = hc-sr04
  LCD1 = LCD screen  # not connected
  U5 = POT [package=pot_alpha_rv16af-20]
  D1 = SOLAR-IXYS [package=solarbit-12x1]
  LED1 = smd LED [color="Red (633nm)" package="0603 [SMD]"]
  LED2 = smd LED [color="Red (633nm)" package="0603 [SMD]"]
  S3 = Pushbutton [package="[SMD]"]
  LED3 = smd LED [color="Red (633nm)" package="0603 [SMD]"]
  S4 = Pushbutton [package="[SMD]"]
  Part3 = Power Cell LiPo Charger/Booster  # not connected
  S6 = SPST Switch [package=ayz0202]  # not connected
  SW1 = DIP SWITCH [package=dipswitch-02]  # not connected

nets:
  N1: L298N1.OUT1, M2.pin_2
  N2: L298N1.OUT2, M2.pin_1
  N3: L298N1.OUT3, M1.pin_2
  N4: L298N1.OUT4, M1.pin_1
  12V: L298N1.12V, Part1.VIN, U1.+
  GND: L298N1.GND, Part1.GND, U2.-, hc-sr1.GND, U5.E
  5V: L298N1.5V, Part1.5V, hc-sr1.VCC, U5.A
  N5: L298N1.ENB, Part1.D5_PWM
  N6: L298N1.IN3, Part1.D7
  N7: L298N1.IN4, Part1.D6_PWM
  N8: Part1.A0, U5.S
  N9: Part1.D9_PWM, hc-sr1.Trig
  N10: Part1.D10_PWM/SS, hc-sr1.Echo
  N11: U1.-, U2.+
  N12: D1.A, LED1.anode, LED2.anode, S3.Pin_3, S3.Pin_4, LED3.anode, S4.Pin_3, S4.Pin_4
  N13: D1.C, LED1.cathode, LED2.cathode, LED3.cathode

notes:
  2 x 3.7 V LiPo Batteries connected in series
  Left Motor
  Right Motor
  L298N Motor Driver Board
  Potentiometer
  LCD Screen
  Solar Panel
  HC SR-04 (SONAR Sensor)
  Lipo charger Module
  Indicator Light
  Head Light

custom parts:
  L298N DC motor driver: 2x DC motor driver with 78M05 positive voltage regulator (7..35 V) L298N: max 46 V, 2 A Set 5 V Enable jumper to enable 5 V regultor (needed for the L298N) and +5 V output at screw terminal or supply external +5 V at screw terminal Set ENA and/or ENB to +5 V to enable motor permanently or supply ENA and/or ENB with PWM signal IN1 and IN2 set rotation directory for motor A (OUT1/OUT2) IN2 and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
